// Logisim project F6.circ as structural Verilog: 2 circuits, main circuit minirv
module minirv (
);

  wire and_1_out, and_2_out, and_3_out, and_4_out, and_5_out, and_6_out, and_7_out, and_8_out, and_9_out,
       clk_out, comparator_1_eq, comparator_2_eq, comparator_3_eq, comparator_4_eq, comparator_5_eq,
       comparator_6_eq, comparator_7_eq, comparator_8_eq, comparator_9_eq, comparator_10_eq,
       comparator_11_eq, comparator_12_eq, comparator_13_eq, comparator_14_eq, comparator_15_eq,
       comparator_16_eq, comparator_17_gt, comparator_18_lt, comparator_19_eq, multiplexer_5_out,
       multiplexer_11_out, not_1_out, por_1_out;
  wire [1:0] adder_1_out;
  wire [2:0] adder_6_out, register_1_q;
  wire [3:0] decoder_1_out0, multiplexer_1_out, multiplexer_6_out, multiplexer_7_out, multiplexer_8_out,
       multiplexer_10_out, priority_encoder_1_out, state_q;
  wire [7:0] multiplexer_2_out, ram_1_dout, ram_1_dout_2, ram_1_dout_3, ram_1_dout_4;
  wire [23:0] adder_1_out_2, multiplexer_4_out;
  wire [31:0] adder_2_out, adder_3_out, adder_4_out, adder_5_out, bit_extender_1_out, bit_extender_2_out,
       bit_extender_3_out, bit_extender_4_out, multiplexer_3_out, multiplexer_9_out, multiplexer_12_out,
       PC_q, rf_1_rd1, rf_1_rd2, rom_1_data;
  wire [31:26] adder_1_out_3;

  Clock clk (.out(clk_out));
  POR por_1 (.out(por_1_out));
  ROM #(.addrWidth(20), .dataWidth(32)) rom_1 (.addr(PC_q[21:2]), .data(rom_1_data));
  Comparator #(.mode("unsigned"), .width(7)) comparator_1 (
    .a(rom_1_data[6:0]), .b(7'b0010011), .eq(comparator_1_eq));  // open: gt, lt
  Comparator #(.mode("unsigned"), .width(3)) comparator_2 (
    .a(rom_1_data[14:12]), .b(3'b000), .eq(comparator_2_eq));  // open: gt, lt
  Comparator #(.mode("unsigned"), .width(7)) comparator_3 (
    .a(rom_1_data[6:0]), .b(7'b1100111), .eq(comparator_3_eq));  // open: gt, lt
  Comparator #(.mode("unsigned"), .width(3)) comparator_4 (
    .a(rom_1_data[14:12]), .b(3'b000), .eq(comparator_4_eq));  // open: gt, lt
  Comparator #(.mode("unsigned"), .width(7)) comparator_5 (
    .a(rom_1_data[6:0]), .b(7'b0110011), .eq(comparator_5_eq));  // open: gt, lt
  Comparator #(.mode("unsigned"), .width(3)) comparator_6 (
    .a(rom_1_data[14:12]), .b(3'b000), .eq(comparator_6_eq));  // open: gt, lt
  Comparator #(.mode("unsigned"), .width(7)) comparator_7 (
    .a(rom_1_data[31:25]), .b({7{1'b0}}), .eq(comparator_7_eq));  // open: gt, lt
  Comparator #(.mode("unsigned"), .width(7)) comparator_8 (
    .a(rom_1_data[6:0]), .b(7'b0110111), .eq(comparator_8_eq));  // open: gt, lt
  Comparator #(.mode("unsigned"), .width(7)) comparator_9 (
    .a(rom_1_data[6:0]), .b(7'b0000011), .eq(comparator_9_eq));  // open: gt, lt
  Comparator #(.mode("unsigned"), .width(3)) comparator_10 (
    .a(rom_1_data[14:12]), .b(3'b010), .eq(comparator_10_eq));  // open: gt, lt
  Comparator #(.mode("unsigned"), .width(7)) comparator_11 (
    .a(rom_1_data[6:0]), .b(7'b0000011), .eq(comparator_11_eq));  // open: gt, lt
  Comparator #(.mode("unsigned"), .width(3)) comparator_12 (
    .a(rom_1_data[14:12]), .b(3'b100), .eq(comparator_12_eq));  // open: gt, lt
  Comparator #(.mode("unsigned"), .width(7)) comparator_13 (
    .a(rom_1_data[6:0]), .b(7'b0100011), .eq(comparator_13_eq));  // open: gt, lt
  Comparator #(.mode("unsigned"), .width(3)) comparator_14 (
    .a(rom_1_data[14:12]), .b(3'b010), .eq(comparator_14_eq));  // open: gt, lt
  Comparator #(.mode("unsigned"), .width(7)) comparator_15 (
    .a(rom_1_data[6:0]), .b(7'b0100011), .eq(comparator_15_eq));  // open: gt, lt
  Comparator #(.mode("unsigned"), .width(3)) comparator_16 (
    .a(rom_1_data[14:12]), .b(3'b000), .eq(comparator_16_eq));  // open: gt, lt
  and and_1 (and_1_out, comparator_1_eq, comparator_2_eq);
  and and_2 (and_2_out, comparator_3_eq, comparator_4_eq);
  and and_3 (and_3_out, comparator_5_eq, comparator_6_eq, comparator_7_eq);
  and and_4 (and_4_out, comparator_9_eq, comparator_10_eq);
  and and_5 (and_5_out, comparator_11_eq, comparator_12_eq);
  and and_6 (and_6_out, comparator_13_eq, comparator_14_eq);
  and and_7 (and_7_out, comparator_15_eq, comparator_16_eq);
  assign bit_extender_1_out = {{20{rom_1_data[31]}}, rom_1_data[31:20]};  // Bit_Extender bit_extender_1
  assign bit_extender_2_out = {{20{rom_1_data[31]}}, {rom_1_data[31:25], rom_1_data[11:7]}};  // Bit_Extender bit_extender_2
  assign bit_extender_3_out = {{20{rom_1_data[31]}}, rom_1_data[31:20]};  // Bit_Extender bit_extender_3
  Priority_Encoder #(.select(4)) priority_encoder_1 (
    .in1(and_1_out), .in2(and_2_out), .in3(and_3_out), .in4(comparator_8_eq), .in5(and_4_out),
    .in6(and_5_out), .in7(and_6_out), .in8(and_7_out), .out(priority_encoder_1_out));  // open: in0, in9, in10, in11, in12, in13, in14, in15, gs, en_out, en_in
  Register #(.width(4)) state (.D(multiplexer_1_out), .en(1'b1), .clk(clk_out), .Q(state_q), .clr(por_1_out));
  Multiplexer #(.select(4), .width(4)) multiplexer_1 (
    .in0(priority_encoder_1_out), .in1(4'b0000), .in2(4'b0000), .in3(4'b0000), .in4(4'b0000), .in5(4'b0000),
    .in6(4'b0000), .in7(4'b0000), .in8(4'b0000), .out(multiplexer_1_out), .sel(state_q));  // open: in9, in10, in11, in12, in13, in14, in15
  Multiplexer #(.select(2), .width(8)) multiplexer_2 (
    .in0(ram_1_dout), .in1(ram_1_dout_2), .in2(ram_1_dout_3), .in3(ram_1_dout_4), .out(multiplexer_2_out),
    .sel(adder_1_out));
  Adder #(.width(32)) adder_1 (
    .a(rf_1_rd1), .b(bit_extender_1_out), .out({adder_1_out_3, adder_1_out_2, adder_1_out}));  // open: cin, cout
  Adder #(.width(32)) adder_2 (.a(rf_1_rd1), .b(bit_extender_2_out), .out(adder_2_out));  // open: cin, cout
  Comparator #(.mode("unsigned"), .width(32)) comparator_17 (
    .a({adder_1_out_3, adder_1_out_2, adder_1_out}), .b(32'h1fffffff), .gt(comparator_17_gt));  // open: eq, lt
  Comparator #(.mode("unsigned"), .width(32)) comparator_18 (
    .a({adder_1_out_3, adder_1_out_2, adder_1_out}), .b(32'h20040001), .lt(comparator_18_lt));  // open: gt, eq
  Decoder #(.select(2)) decoder_1 (
    .out0(decoder_1_out0[0]), .out1(decoder_1_out0[1]), .out2(decoder_1_out0[2]), .out3(decoder_1_out0[3]),
    .sel(adder_2_out[1:0]), .en(1'b1));
  and and_8 (and_8_out, comparator_17_gt, comparator_18_lt);
  Adder #(.width(32)) adder_3 (.a(rf_1_rd2), .b(rf_1_rd1), .out(adder_3_out));  // open: cin, cout
  assign bit_extender_4_out = {{24{1'b0}}, multiplexer_2_out};  // Bit_Extender bit_extender_4
  Adder #(.width(32)) adder_4 (.a(rf_1_rd1), .b(bit_extender_3_out), .out(adder_4_out));  // open: cin, cout
  Adder #(.width(32)) adder_5 (.a(32'h4), .b(PC_q), .out(adder_5_out));  // open: cin, cout
  not not_1 (not_1_out, and_8_out);
  Multiplexer #(.select(4), .width(32)) multiplexer_3 (
    .in7(rf_1_rd2), .in8({rf_1_rd2[7:0], rf_1_rd2[7:0], rf_1_rd2[7:0], rf_1_rd2[7:0]}),
    .out(multiplexer_3_out), .sel(state_q));  // open: in0, in1, in2, in3, in4, in5, in6, in9, in10, in11, in12, in13, in14, in15
  Multiplexer #(.select(4), .width(24)) multiplexer_4 (
    .in5(adder_1_out_2), .in6(adder_1_out_2), .in7(adder_2_out[25:2]), .in8(adder_2_out[25:2]),
    .out(multiplexer_4_out), .sel(state_q));  // open: in0, in1, in2, in3, in4, in9, in10, in11, in12, in13, in14, in15
  Multiplexer #(.select(4)) multiplexer_5 (
    .in0(1'b0), .in1(1'b0), .in2(1'b0), .in3(1'b0), .in4(1'b0), .in5(1'b0), .in6(1'b0), .in7(not_1_out),
    .in8(1'b1), .out(multiplexer_5_out), .sel(state_q));  // open: in9, in10, in11, in12, in13, in14, in15
  Multiplexer #(.select(4), .width(4)) multiplexer_6 (
    .in5(4'b1111), .in6(4'b1111), .in7(4'b1111), .in8(decoder_1_out0), .out(multiplexer_6_out), .sel(state_q));  // open: in0, in1, in2, in3, in4, in9, in10, in11, in12, in13, in14, in15
  Multiplexer #(.select(4), .width(4)) multiplexer_7 (
    .in3(rom_1_data[23:20]), .in7(rom_1_data[23:20]), .in8(rom_1_data[23:20]), .out(multiplexer_7_out),
    .sel(state_q));  // open: in0, in1, in2, in4, in5, in6, in9, in10, in11, in12, in13, in14, in15
  Multiplexer #(.select(4), .width(4)) multiplexer_8 (
    .in1(rom_1_data[18:15]), .in2(rom_1_data[18:15]), .in3(rom_1_data[18:15]), .in5(rom_1_data[18:15]),
    .in6(rom_1_data[18:15]), .in7(rom_1_data[18:15]), .in8(rom_1_data[18:15]), .out(multiplexer_8_out),
    .sel(state_q));  // open: in0, in4, in9, in10, in11, in12, in13, in14, in15
  Multiplexer #(.select(4), .width(32)) multiplexer_9 (
    .in1(adder_4_out), .in2(adder_5_out), .in3(adder_3_out), .in4({rom_1_data[31:12], {12{1'b0}}}),
    .in5({ram_1_dout_4, ram_1_dout_3, ram_1_dout_2, ram_1_dout}), .in6(bit_extender_4_out),
    .out(multiplexer_9_out), .sel(state_q));  // open: in0, in7, in8, in9, in10, in11, in12, in13, in14, in15
  Multiplexer #(.select(4), .width(4)) multiplexer_10 (
    .in1(rom_1_data[10:7]), .in2(rom_1_data[10:7]), .in3(rom_1_data[10:7]), .in4(rom_1_data[10:7]),
    .in5(rom_1_data[10:7]), .in6(rom_1_data[10:7]), .out(multiplexer_10_out), .sel(state_q));  // open: in0, in7, in8, in9, in10, in11, in12, in13, in14, in15
  Multiplexer #(.select(4)) multiplexer_11 (
    .in0(1'b0), .in1(1'b1), .in2(1'b1), .in3(1'b1), .in4(1'b1), .in5(1'b1), .in6(1'b1), .in7(1'b0),
    .in8(1'b0), .out(multiplexer_11_out), .sel(state_q));  // open: in9, in10, in11, in12, in13, in14, in15
  Multiplexer #(.select(4), .width(32)) multiplexer_12 (
    .in0(PC_q), .in1(adder_5_out), .in2({adder_4_out[31:1], 1'b0}), .in3(adder_5_out), .in4(adder_5_out),
    .in5(adder_5_out), .in6(adder_5_out), .in7(adder_5_out), .in8(adder_5_out), .out(multiplexer_12_out),
    .sel(state_q));  // open: in9, in10, in11, in12, in13, in14, in15
  Register #(.width(32)) PC (.D(multiplexer_12_out), .en(1'b1), .clk(clk_out), .Q(PC_q), .clr(por_1_out));
  RAM #(.addrWidth(24), .asyncread("true"), .byteenables("byteEnables"), .dataWidth(32), .\type ("nonvolatile")) ram_1 (
    .addr(multiplexer_4_out), .we(multiplexer_5_out), .oe(1'b1), .clk(clk_out), .din(multiplexer_3_out),
    .dout({ram_1_dout_4, ram_1_dout_3, ram_1_dout_2, ram_1_dout}), .be3(multiplexer_6_out[3]),
    .be2(multiplexer_6_out[2]), .be1(multiplexer_6_out[1]), .be0(multiplexer_6_out[0]));
  Comparator #(.mode("unsigned"), .width(4)) comparator_19 (
    .a(4'b0111), .b(state_q), .eq(comparator_19_eq));  // open: gt, lt
  Register #(.width(3)) register_1 (.D(adder_6_out), .en(and_9_out), .clk(clk_out), .Q(register_1_q), .clr(por_1_out));
  and and_9 (and_9_out, and_8_out, comparator_19_eq);
  RF rf_1 (
    .r_addr2(multiplexer_7_out), .r_addr1(multiplexer_8_out), .w_data(multiplexer_9_out),
    .w_addr(multiplexer_10_out), .we(multiplexer_11_out), .clk(clk_out), .rst(por_1_out), .rd2(rf_1_rd2),
    .rd1(rf_1_rd1));
  Adder #(.width(3)) adder_6 (.a(register_1_q), .b(3'b001), .out(adder_6_out));  // open: cin, cout
  // RGB_Video #(.cursor("No Cursor"), .height(256), .width(256)) rgb_video_1: pin names not known; wires that end beside it: por_1_out, clk_out, and_9_out, {adder_1_out_2[7:3], register_1_q}, adder_1_out_2[15:8], rf_1_rd2[23:0]

  // Notes on the sheet:
  //   contents of rom_1 (hex, n*v repeats v):
  //   413 93137 10113 10b7 dbc08093 80e7 fe012823 fea10923 fea12423 fe914203 fe4109a3 ff012783 f787b3
  //   f787b3 4b6b7 af868693 fdc10113 d787b3 10000713 f12423 10593 100793 b00513 2112023 12023 12223 e12623
  //   e12823 f10a23 10b7 a8408093 80e7 2012083 2410113 8067 ff410113 112423 10b7 a7c08093 80e7 513 1800093
  //   80e7 812083 513 c10113 8067 852583 feb12823 fe812e23 3437 80840413 ff014183 3401b3 1c183 ff114203
  //   440233 24203 4181b3 ff214203 440233 24203 4181b3 ff314203 440233 24203 4181b3 3237 80020213 320233
  //   24203 ffc12403 420233 420233 410233 11b7 86418193 fe312823 14800193 fe312623 fec22203 20067 1052703
  //   52683 452783 fe810113 e12423 112a23 812823 912623 fed12823 fef12623 13737 a0070713 fe012223 ff314203
  //   fe4102a3 fef14203 fe410223 fe412203 470233 24203 fe4105a3 ff214203 fe4102a3 fee14203 fe410223
  //   fe412203 470233 24203 fe410523 ff114203 fe4102a3 fed14203 fe410223 fe412203 470233 24203 fe4104a3
  //   ff014203 fe4102a3 fec14203 fe410223 fe412203 470233 24203 fe410423 fe812703 c52603 fee12823 fe812e23
  //   3437 80840413 ff014183 3401b3 1c183 ff114203 440233 24203 4181b3 ff214203 440233 24203 4181b3
  //   ff314203 440233 24203 4181b3 3237 80020213 320233 24203 ffc12403 420233 420233 410233 66800193
  //   fe312823 28800193 fe312623 fec22203 20067 c68733 10000513 fe812e23 fe912c23 fee12823 50413 ff012483
  //   fe812423 feb14183 3181b3 fe312423 fe914183 3181b3 fe912423 feb14203 420233 fe412423 fe914203 4181b3
  //   3181b3 fe312a23 fe912423 33237 90020213 feb14183 4181b3 1c183 fe3103a3 fea14183 4181b3 1c183
  //   fe310323 fe914183 4181b3 1c183 fe3102a3 fe814183 4181b3 1c183 fe310223 ff412183 fe412203 440233
  //   120213 fe412423 feb14203 420233 fe412423 fe914203 4181b3 3237 90820213 320233 ff812483 ffc12403
  //   24203 420233 420233 410233 11b7 86818193 fe312823 39000193 fe312623 fec22203 20067 812703 10000513
  //   e78733 fe812e23 fe912c23 fee12823 50413 ff012483 fe812423 feb14183 3181b3 fe312423 fe914183 3181b3
  //   fe912423 feb14203 420233 fe412423 fe914203 4181b3 3181b3 fe312a23 fe912423 33237 90020213 feb14183
  //   4181b3 1c183 fe3103a3 fea14183 4181b3 1c183 fe310323 fe914183 4181b3 1c183 fe3102a3 fe814183 4181b3
  //   1c183 fe310223 ff412183 fe412203 440233 120213 fe412423 feb14203 420233 fe412423 fe914203 4181b3
  //   3237 90820213 320233 ff812483 ffc12403 24203 420233 420233 410233 11b7 86818193 fe312823 49c00193
  //   fe312623 fec22203 20067 8*f787b3 d787b3 f787b3 f787b3 20000437 f40433 812783 c60633 c60633 fef12423
  //   feb14183 3181b3 fe312423 fe914183 fff78213 fe412423 feb14203 420233 fe412423 fe914203 4181b3 3237
  //   91820213 418233 24203 420233 420233 410233 65400193 fe312823 54000193 fe312623 fec22203 20067 493
  //   40513 b12223 c12023 10b7 de008093 80e7 12603 412583 812783 148493 40040413 c585b3 fef12823 fe912623
  //   fe812e23 fe912c23 2437 70040413 ff014183 340233 100193 320023 fec14183 3401b3 18023 24183 ff114483
  //   940233 100493 920023 fed14483 9404b3 48023 24483 9181b3 ff214483 940233 100493 920023 fee14483
  //   9404b3 48023 24483 9181b3 ff314483 940233 100493 920023 fef14483 9404b3 48023 24483 9181b3 3237
  //   80020213 320233 24203 ff812483 ffc12403 420233 420233 410233 65400193 fe312823 54400193 fe312623
  //   fec22203 20067 1412083 1012403 c12483 1810113 8067 10000713 fec12823 fee12623 fe812e23 fe912c23 2437
  //   70040413 ff014183 340233 100193 320023 fec14183 3401b3 18023 24183 ff114483 940233 100493 920023
  //   fed14483 9404b3 48023 24483 9181b3 ff214483 940233 100493 920023 fee14483 9404b3 48023 24483 9181b3
  //   ff314483 940233 100493 920023 fef14483 9404b3 48023 24483 9181b3 3237 80020213 320233 24203 ff812483
  //   ffc12403 420233 420233 410233 74c00193 fe312823 28800193 fe312623 fec22203 20067 812703 fee12823
  //   fec12623 fe812e23 fe912c23 2437 70040413 ff014183 340233 100193 320023 fec14183 3401b3 18023 24183
  //   ff114483 940233 100493 920023 fed14483 9404b3 48023 24483 9181b3 ff214483 940233 100493 920023
  //   fee14483 9404b3 48023 24483 9181b3 ff314483 940233 100493 920023 fef14483 9404b3 48023 24483 9181b3
  //   3237 80020213 320233 24203 ff812483 ffc12403 420233 420233 410233 11b7 83418193 fe312823 39000193
  //   fe312623 fec22203 20067 1012403 1412083 c12483 40637 20000537 1810113 1237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
  //   ADDI
  //   JALR
  //   ADD
  //   LUI
  //   LW
  //   LBU
  //   SW
  //   SB
endmodule

module RF (
  input  [3:0] r_addr2,
  input  [3:0] r_addr1,
  input  [31:0] w_data,
  input  [3:0] w_addr,
  input  we,
  input  clk,
  input  rst,
  output [31:0] rd2,
  output [31:0] rd1
);

  wire decoder_1_out0, decoder_1_out1, decoder_1_out2, decoder_1_out3, decoder_1_out4, decoder_1_out5,
       decoder_1_out6, decoder_1_out7, decoder_1_out8, decoder_1_out9, decoder_1_out10, decoder_1_out11,
       decoder_1_out12, decoder_1_out13, decoder_1_out14, decoder_1_out15;
  wire [31:0] register_1_q, register_2_q, register_3_q, register_4_q, register_5_q, register_6_q,
       register_7_q, register_8_q, register_9_q, register_10_q, register_11_q, register_12_q, register_13_q,
       register_14_q, register_15_q, register_16_q;

  Decoder #(.select(4)) decoder_1 (
    .out0(decoder_1_out0), .out1(decoder_1_out1), .out2(decoder_1_out2), .out3(decoder_1_out3),
    .out4(decoder_1_out4), .out5(decoder_1_out5), .out6(decoder_1_out6), .out7(decoder_1_out7),
    .out8(decoder_1_out8), .out9(decoder_1_out9), .out10(decoder_1_out10), .out11(decoder_1_out11),
    .out12(decoder_1_out12), .out13(decoder_1_out13), .out14(decoder_1_out14), .out15(decoder_1_out15),
    .sel(w_addr), .en(we));
  Register #(.width(32)) register_1 (.D({32{1'b0}}), .en(decoder_1_out0), .clk(clk), .Q(register_1_q), .clr(rst));
  Register #(.width(32)) register_2 (.D(w_data), .en(decoder_1_out1), .clk(clk), .Q(register_2_q), .clr(rst));
  Register #(.width(32)) register_3 (.D(w_data), .en(decoder_1_out2), .clk(clk), .Q(register_3_q), .clr(rst));
  Register #(.width(32)) register_4 (.D(w_data), .en(decoder_1_out3), .clk(clk), .Q(register_4_q), .clr(rst));
  Register #(.width(32)) register_5 (.D(w_data), .en(decoder_1_out4), .clk(clk), .Q(register_5_q), .clr(rst));
  Register #(.width(32)) register_6 (.D(w_data), .en(decoder_1_out5), .clk(clk), .Q(register_6_q), .clr(rst));
  Register #(.width(32)) register_7 (.D(w_data), .en(decoder_1_out6), .clk(clk), .Q(register_7_q), .clr(rst));
  Register #(.width(32)) register_8 (.D(w_data), .en(decoder_1_out7), .clk(clk), .Q(register_8_q), .clr(rst));
  Register #(.width(32)) register_9 (.D(w_data), .en(decoder_1_out8), .clk(clk), .Q(register_9_q), .clr(rst));
  Register #(.width(32)) register_10 (.D(w_data), .en(decoder_1_out9), .clk(clk), .Q(register_10_q), .clr(rst));
  Register #(.width(32)) register_11 (.D(w_data), .en(decoder_1_out10), .clk(clk), .Q(register_11_q), .clr(rst));
  Register #(.width(32)) register_12 (.D(w_data), .en(decoder_1_out11), .clk(clk), .Q(register_12_q), .clr(rst));
  Register #(.width(32)) register_13 (.D(w_data), .en(decoder_1_out12), .clk(clk), .Q(register_13_q), .clr(rst));
  Register #(.width(32)) register_14 (.D(w_data), .en(decoder_1_out13), .clk(clk), .Q(register_14_q), .clr(rst));
  Register #(.width(32)) register_15 (.D(w_data), .en(decoder_1_out14), .clk(clk), .Q(register_15_q), .clr(rst));
  Register #(.width(32)) register_16 (.D(w_data), .en(decoder_1_out15), .clk(clk), .Q(register_16_q), .clr(rst));
  Multiplexer #(.select(4), .width(32)) multiplexer_1 (
    .in0(register_1_q), .in1(register_2_q), .in2(register_3_q), .in3(register_4_q), .in4(register_5_q),
    .in5(register_6_q), .in6(register_7_q), .in7(register_8_q), .in8(register_9_q), .in9(register_10_q),
    .in10(register_11_q), .in11(register_12_q), .in12(register_13_q), .in13(register_14_q),
    .in14(register_15_q), .in15(register_16_q), .out(rd2), .sel(r_addr2));
  Multiplexer #(.select(4), .width(32)) multiplexer_2 (
    .in0(register_1_q), .in1(register_2_q), .in2(register_3_q), .in3(register_4_q), .in4(register_5_q),
    .in5(register_6_q), .in6(register_7_q), .in7(register_8_q), .in8(register_9_q), .in9(register_10_q),
    .in10(register_11_q), .in11(register_12_q), .in12(register_13_q), .in13(register_14_q),
    .in14(register_15_q), .in15(register_16_q), .out(rd1), .sel(r_addr1));
endmodule
